# Fritzing sketch jf_sample (saved by Fritzing 0.9.2b)
breadboards: 1

parts:
  パーツ1 = Arduino Uno (Rev3)
  LED1 = LED - 5mm [color="Red (633nm)" package="5 mm [THT]"]
  R1 = Resistor [tolerance=±5% resistance=150 package=THT]

nets:
  N1: パーツ1.D13/SCK, R1.Pin_0
  N2: パーツ1.GND, LED1.cathode
  N3: LED1.anode, R1.Pin_1
